// Logisim project 01_ROM.circ as structural Verilog: 1 circuit, main circuit main
module main (
  input  [4:0] in_1,
  output [11:0] out_2
);

  ROM #(.addrWidth(5), .dataWidth(12)) rom_1 (.addr(in_1), .data(out_2));

  // Notes on the sheet:
  //   contents of rom_1 (hex, n*v repeats v):
  //   11 1 0 1 0 1 0 1 0 111 0 1 100 11 0 100 1 0 101 0 101 111 0 0 1 0 0 101 0 1 0 111
endmodule
