// Logisim project 02_RAM.circ as structural Verilog: 1 circuit, main circuit main
module main (
  input  [4:0] in_1,
  input  in_2,
  input  in_3,
  input  in_4,
  output [11:0] out_5
);

  RAM #(.addrWidth(5), .asyncread("true"), .dataWidth(12)) ram_1 (
    .addr(in_1), .we(in_2), .oe(in_3), .clk(in_4), .dout(out_5));  // open: din
endmodule
