// Logisim project 03_RAM.circ as structural Verilog: 1 circuit, main circuit main
module main (
  input  [7:0] Endereco,
  input  [3:0] DataIn,
  input  Load,
  input  CLK
);

  wire and_1_out, and_2_out, not_1_out;

  not not_1 (not_1_out, Endereco[7]);
  and and_1 (and_1_out, not_1_out, Load);
  and and_2 (and_2_out, Endereco[7], Load);
  RAM #(.addrWidth(7), .dataWidth(4)) RAM_0A (
    .addr(Endereco[6:0]), .we(and_1_out), .oe(1'b1), .clk(CLK), .din(DataIn));  // open: dout
  RAM #(.addrWidth(7), .dataWidth(4)) ram_1 (
    .addr(Endereco[6:0]), .we(and_1_out), .oe(1'b1), .clk(CLK), .din(DataIn));  // open: dout
  RAM #(.addrWidth(7), .dataWidth(4)) ram_2 (
    .addr(Endereco[6:0]), .we(and_2_out), .oe(1'b1), .clk(CLK), .din(DataIn));  // open: dout
  RAM #(.addrWidth(7), .dataWidth(4)) ram_3 (
    .addr(Endereco[6:0]), .we(and_2_out), .oe(1'b1), .clk(CLK), .din(DataIn));  // open: dout
endmodule
