// Logisim project 05_RAM.circ as structural Verilog: 1 circuit, main circuit main
module main (
  input  [2:0] in_1,
  input  WE,
  input  D3,
  input  D2,
  input  D1,
  input  D0
);

  wire and_1_out, and_2_out, and_3_out, and_4_out, and_5_out, and_6_out, and_7_out, and_8_out,
       decoder_1_out0, decoder_1_out1, decoder_1_out2, decoder_1_out3, decoder_1_out4, decoder_1_out5,
       decoder_1_out6, decoder_1_out7;

  Decoder #(.select(3)) decoder_1 (
    .out0(decoder_1_out0), .out1(decoder_1_out1), .out2(decoder_1_out2), .out3(decoder_1_out3),
    .out4(decoder_1_out4), .out5(decoder_1_out5), .out6(decoder_1_out6), .out7(decoder_1_out7), .sel(in_1));  // open: en
  and and_1 (and_1_out, decoder_1_out0, WE);
  and and_2 (and_2_out, decoder_1_out1, WE);
  and and_3 (and_3_out, decoder_1_out2, WE);
  and and_4 (and_4_out, decoder_1_out3, WE);
  and and_5 (and_5_out, decoder_1_out4, WE);
  and and_6 (and_6_out, decoder_1_out5, WE);
  and and_7 (and_7_out, decoder_1_out6, WE);
  and and_8 (and_8_out, decoder_1_out7, WE);
  D_Flip_Flop d_ff_1 (.D(D3), .clk(and_1_out));  // open: Q, Qn, preset, reset
  D_Flip_Flop d_ff_2 (.D(D3), .clk(and_2_out));  // open: Q, Qn, preset, reset
  D_Flip_Flop d_ff_3 (.clk(and_3_out));  // open: D, Q, Qn, preset, reset
  D_Flip_Flop d_ff_4 (.clk(and_4_out));  // open: D, Q, Qn, preset, reset
  D_Flip_Flop d_ff_5 (.D(D3), .clk(and_5_out));  // open: Q, Qn, preset, reset
  D_Flip_Flop d_ff_6 (.D(D3), .clk(and_6_out));  // open: Q, Qn, preset, reset
  D_Flip_Flop d_ff_7 (.D(D3), .clk(and_7_out));  // open: Q, Qn, preset, reset
  D_Flip_Flop d_ff_8 (.D(D3), .clk(and_8_out));  // open: Q, Qn, preset, reset
  D_Flip_Flop d_ff_9 (.D(D2), .clk(and_1_out));  // open: Q, Qn, preset, reset
  D_Flip_Flop d_ff_10 (.D(D2), .clk(and_2_out));  // open: Q, Qn, preset, reset
  D_Flip_Flop d_ff_11 (.D(D2), .clk(and_3_out));  // open: Q, Qn, preset, reset
  D_Flip_Flop d_ff_12 (.D(D2), .clk(and_4_out));  // open: Q, Qn, preset, reset
  D_Flip_Flop d_ff_13 (.D(D2), .clk(and_5_out));  // open: Q, Qn, preset, reset
  D_Flip_Flop d_ff_14 (.D(D2), .clk(and_6_out));  // open: Q, Qn, preset, reset
  D_Flip_Flop d_ff_15 (.D(D2), .clk(and_7_out));  // open: Q, Qn, preset, reset
  D_Flip_Flop d_ff_16 (.D(D2), .clk(and_8_out));  // open: Q, Qn, preset, reset
  D_Flip_Flop d_ff_17 (.D(D1), .clk(and_1_out));  // open: Q, Qn, preset, reset
  D_Flip_Flop d_ff_18 (.D(D1), .clk(and_2_out));  // open: Q, Qn, preset, reset
  D_Flip_Flop d_ff_19 (.D(D1), .clk(and_3_out));  // open: Q, Qn, preset, reset
  D_Flip_Flop d_ff_20 (.D(D1), .clk(and_4_out));  // open: Q, Qn, preset, reset
  D_Flip_Flop d_ff_21 (.D(D1), .clk(and_5_out));  // open: Q, Qn, preset, reset
  D_Flip_Flop d_ff_22 (.D(D1), .clk(and_6_out));  // open: Q, Qn, preset, reset
  D_Flip_Flop d_ff_23 (.D(D1), .clk(and_7_out));  // open: Q, Qn, preset, reset
  D_Flip_Flop d_ff_24 (.D(D1), .clk(and_8_out));  // open: Q, Qn, preset, reset
  D_Flip_Flop d_ff_25 (.D(D0), .clk(and_1_out));  // open: Q, Qn, preset, reset
  D_Flip_Flop d_ff_26 (.clk(and_2_out));  // open: D, Q, Qn, preset, reset
  D_Flip_Flop d_ff_27 (.D(D0), .clk(and_3_out));  // open: Q, Qn, preset, reset
  D_Flip_Flop d_ff_28 (.clk(and_4_out));  // open: D, Q, Qn, preset, reset
  D_Flip_Flop d_ff_29 (.D(D0), .clk(and_5_out));  // open: Q, Qn, preset, reset
  D_Flip_Flop d_ff_30 (.D(D0), .clk(and_6_out));  // open: Q, Qn, preset, reset
  D_Flip_Flop d_ff_31 (.D(D0), .clk(and_7_out));  // open: Q, Qn, preset, reset
  D_Flip_Flop d_ff_32 (.D(D0), .clk(and_8_out));  // open: Q, Qn, preset, reset
endmodule
