// Logisim project 06_ROM.circ as structural Verilog: 1 circuit, main circuit main
module main (
  input  [2:0] in_1,
  input  OE,
  output S3,
  output S2,
  output S1,
  output S0
);

  wire D0_out, D1_out, D2_out, D3_out, decoder_1_out5, decoder_1_out6, pull_resistor_1_node,
       pull_resistor_2_node, pull_resistor_3_node, pull_resistor_4_node, pull_resistor_5_node,
       pull_resistor_10_node;

  Pull_Resistor pull_resistor_1 (.node(pull_resistor_1_node));
  Pull_Resistor pull_resistor_2 (.node(pull_resistor_2_node));
  Pull_Resistor pull_resistor_3 (.node(pull_resistor_3_node));
  Pull_Resistor pull_resistor_4 (.node(pull_resistor_4_node));
  Pull_Resistor pull_resistor_5 (.node(pull_resistor_5_node));
  Pull_Resistor pull_resistor_6 (.node(pull_resistor_3_node));
  Pull_Resistor pull_resistor_7 (.node(pull_resistor_4_node));
  Pull_Resistor pull_resistor_8 (.node(pull_resistor_4_node));
  Pull_Resistor pull_resistor_9 (.node(pull_resistor_3_node));
  Pull_Resistor pull_resistor_10 (.node(pull_resistor_10_node));
  Pull_Resistor pull_resistor_11 (.node(pull_resistor_10_node));
  Pull_Resistor pull_resistor_12 (.node(pull_resistor_1_node));
  Pull_Resistor pull_resistor_13 (.node(pull_resistor_4_node));
  Pull_Resistor pull_resistor_14 (.node(pull_resistor_5_node));
  Pull_Resistor pull_resistor_15 (.node(pull_resistor_3_node));
  Decoder #(.select(3)) decoder_1 (
    .out0(pull_resistor_10_node), .out1(pull_resistor_1_node), .out2(pull_resistor_2_node),
    .out3(pull_resistor_5_node), .out4(pull_resistor_3_node), .out5(decoder_1_out5), .out6(decoder_1_out6),
    .out7(pull_resistor_4_node), .sel(in_1));  // open: en
  or D3 (D3_out, pull_resistor_1_node, pull_resistor_2_node, pull_resistor_3_node, pull_resistor_4_node);
  or D2 (D2_out, pull_resistor_5_node, pull_resistor_3_node, pull_resistor_4_node);
  or D1 (D1_out, pull_resistor_4_node, pull_resistor_3_node, pull_resistor_5_node, pull_resistor_10_node);
  or D0 (D0_out, pull_resistor_10_node, pull_resistor_1_node, pull_resistor_4_node, pull_resistor_5_node, pull_resistor_3_node);
  assign S3 = OE ? D3_out : 1'bz;  // Controlled_Buffer controlled_buffer_1
  assign S2 = OE ? D2_out : 1'bz;  // Controlled_Buffer controlled_buffer_2
  assign S1 = OE ? D1_out : 1'bz;  // Controlled_Buffer controlled_buffer_3
  assign S0 = OE ? D0_out : 1'bz;  // Controlled_Buffer controlled_buffer_4
endmodule
