// Logisim project 07_RNG.circ as structural Verilog: 1 circuit, main circuit main
module main (
  input  in_1,
  input  in_2
);

  wire clock_1_out;
  wire [7:0] counter_1_q;
  wire [15:0] random_1_out;

  Clock clock_1 (.out(clock_1_out));
  Random #(.width(16)) random_1 (.next(in_2), .clk(clock_1_out), .out(random_1_out));  // open: clr
  Counter counter_1 (.load(in_1), .up(in_2), .clk(clock_1_out), .Q(counter_1_q));  // open: clr, count, D, carry
  RAM #(.dataWidth(16)) ram_1 (
    .addr(counter_1_q), .we(1'b1), .oe(1'b1), .clk(clock_1_out), .din(random_1_out));  // open: dout
endmodule
