// Logisim project 08_7seg.circ as structural Verilog: 1 circuit, main circuit main
module main (
  input  WE,
  input  RST,
  input  [7:0] DataIn,
  input  [15:0] ADDR
);

  wire and_1_out, and_2_out, CLK_out, decoder_1_out0, decoder_1_out1, decoder_1_out2, decoder_1_out3,
       decoder_1_out4, decoder_1_out5, decoder_1_out6, decoder_1_out7;
  wire [7:0] controlled_buffer_1_out, controlled_buffer_7_out, pull_resistor_2_node, pull_resistor_3_node,
       pull_resistor_4_node, pull_resistor_5_node, pull_resistor_6_node, pull_resistor_8_node, register_1_q,
       register_2_q, register_3_q, register_4_q, register_5_q, register_6_q, register_7_q, register_8_q;

  Decoder #(.select(3)) decoder_1 (
    .out0(decoder_1_out0), .out1(decoder_1_out1), .out2(decoder_1_out2), .out3(decoder_1_out3),
    .out4(decoder_1_out4), .out5(decoder_1_out5), .out6(decoder_1_out6), .out7(decoder_1_out7),
    .sel(ADDR[2:0]));  // open: en
  and and_1 (and_1_out, ADDR[3], ADDR[4], ADDR[5], ADDR[6], ADDR[7], ADDR[8], ADDR[9], ADDR[10], ADDR[11], ADDR[12], ADDR[13], ADDR[14], ADDR[15]);
  and and_2 (and_2_out, WE, and_1_out);
  Clock CLK (.out(CLK_out));
  assign controlled_buffer_1_out = decoder_1_out0 ? DataIn : 8'bz;  // Controlled_Buffer controlled_buffer_1
  Register register_1 (.D(controlled_buffer_1_out), .en(and_2_out), .clk(CLK_out), .Q(register_1_q), .clr(RST));
  Pull_Resistor pull_resistor_1 (.node(controlled_buffer_1_out));
  _7_Segment_Display u_7_segment_display_1 (
    .g(register_1_q[0]), .f(register_1_q[1]), .a(register_1_q[2]), .b(register_1_q[3]), .e(register_1_q[4]),
    .d(register_1_q[5]), .c(register_1_q[6]), .dp(register_1_q[7]));
  Register register_2 (.D(pull_resistor_2_node), .en(and_2_out), .clk(CLK_out), .Q(register_2_q), .clr(RST));
  Pull_Resistor pull_resistor_2 (.node(pull_resistor_2_node));
  assign pull_resistor_2_node = decoder_1_out1 ? DataIn : 8'bz;  // Controlled_Buffer controlled_buffer_2
  _7_Segment_Display u_7_segment_display_2 (
    .g(register_2_q[1]), .f(register_2_q[0]), .a(register_2_q[2]), .b(register_2_q[3]), .e(register_2_q[4]),
    .d(register_2_q[5]), .c(register_2_q[6]), .dp(register_2_q[7]));
  Register register_3 (.D(pull_resistor_3_node), .en(and_2_out), .clk(CLK_out), .Q(register_3_q), .clr(RST));
  Pull_Resistor pull_resistor_3 (.node(pull_resistor_3_node));
  assign pull_resistor_3_node = decoder_1_out2 ? DataIn : 8'bz;  // Controlled_Buffer controlled_buffer_3
  _7_Segment_Display u_7_segment_display_3 (
    .g(register_3_q[1]), .f(register_3_q[0]), .a(register_3_q[2]), .b(register_3_q[3]), .e(register_3_q[4]),
    .d(register_3_q[5]), .c(register_3_q[6]), .dp(register_3_q[7]));
  Register register_4 (.D(pull_resistor_4_node), .en(and_2_out), .clk(CLK_out), .Q(register_4_q), .clr(RST));
  Pull_Resistor pull_resistor_4 (.node(pull_resistor_4_node));
  assign pull_resistor_4_node = decoder_1_out3 ? DataIn : 8'bz;  // Controlled_Buffer controlled_buffer_4
  Register register_5 (.D(pull_resistor_5_node), .en(and_2_out), .clk(CLK_out), .Q(register_5_q), .clr(RST));
  Pull_Resistor pull_resistor_5 (.node(pull_resistor_5_node));
  assign pull_resistor_5_node = decoder_1_out4 ? DataIn : 8'bz;  // Controlled_Buffer controlled_buffer_5
  _7_Segment_Display u_7_segment_display_4 (
    .g(register_4_q[1]), .f(register_4_q[0]), .a(register_4_q[2]), .b(register_4_q[3]), .e(register_4_q[4]),
    .d(register_4_q[5]), .c(register_4_q[6]), .dp(register_4_q[7]));
  Pull_Resistor pull_resistor_6 (.node(pull_resistor_6_node));
  assign pull_resistor_6_node = decoder_1_out5 ? DataIn : 8'bz;  // Controlled_Buffer controlled_buffer_6
  _7_Segment_Display u_7_segment_display_5 (
    .g(register_5_q[1]), .f(register_5_q[0]), .a(register_5_q[2]), .b(register_5_q[3]), .e(register_5_q[4]),
    .d(register_5_q[5]), .c(register_5_q[6]), .dp(register_5_q[7]));
  Register register_6 (.D(pull_resistor_6_node), .en(and_2_out), .clk(CLK_out), .Q(register_6_q), .clr(RST));
  assign controlled_buffer_7_out = decoder_1_out6 ? DataIn : 8'bz;  // Controlled_Buffer controlled_buffer_7
  _7_Segment_Display u_7_segment_display_6 (
    .g(register_6_q[1]), .f(register_6_q[0]), .a(register_6_q[2]), .b(register_6_q[3]), .e(register_6_q[4]),
    .d(register_6_q[5]), .c(register_6_q[6]), .dp(register_6_q[7]));
  Register register_7 (.D(controlled_buffer_7_out), .en(and_2_out), .clk(CLK_out), .Q(register_7_q), .clr(RST));
  Pull_Resistor pull_resistor_7 (.node(controlled_buffer_7_out));
  _7_Segment_Display u_7_segment_display_7 (
    .g(register_7_q[1]), .f(register_7_q[0]), .a(register_7_q[2]), .b(register_7_q[3]), .e(register_7_q[4]),
    .d(register_7_q[5]), .c(register_7_q[6]), .dp(register_7_q[7]));
  Register register_8 (.D(pull_resistor_8_node), .en(and_2_out), .clk(CLK_out), .Q(register_8_q), .clr(RST));
  Pull_Resistor pull_resistor_8 (.node(pull_resistor_8_node));
  assign pull_resistor_8_node = decoder_1_out7 ? DataIn : 8'bz;  // Controlled_Buffer controlled_buffer_8
  _7_Segment_Display u_7_segment_display_8 (
    .g(register_8_q[1]), .f(register_8_q[0]), .a(register_8_q[2]), .b(register_8_q[3]), .e(register_8_q[4]),
    .d(register_8_q[5]), .c(register_8_q[6]), .dp(register_8_q[7]));
endmodule
