// Logisim project 09_buzzer.circ as structural Verilog: 1 circuit, main circuit main
module main (
  input  CLK
);

  wire and_1_out, and_2_out, and_3_out, and_4_out, and_5_out, and_6_out, and_7_out, and_8_out, and_9_out,
       and_10_out, and_11_out, and_12_out, and_13_out, not_1_out, not_2_out, not_3_out, or_1_out, or_2_out,
       or_3_out, Q0_q, Q1_q, Q2_q, random_1_out;
  wire [6:0] multiplexer_1_out;

  Random #(.width(1)) random_1 (.next(1'b1), .clk(CLK), .out(random_1_out));  // open: clr
  Multiplexer #(.width(7)) multiplexer_1 (
    .in0(7'b0110000), .in1(7'b0110001), .out(multiplexer_1_out), .sel(random_1_out));
  TTY tty_1 (.data(multiplexer_1_out), .clk(CLK), .we(1'b1), .clr(and_13_out));
  not not_1 (not_1_out, Q2_q);
  not not_2 (not_2_out, Q1_q);
  not not_3 (not_3_out, Q0_q);
  and and_1 (and_1_out, ~random_1_out, not_1_out, not_2_out, not_3_out);  // AND_Gate
  and and_2 (and_2_out, not_1_out, not_2_out, Q0_q, random_1_out);
  and and_3 (and_3_out, not_1_out, Q1_q, random_1_out);
  and and_4 (and_4_out, Q2_q, not_2_out, random_1_out);
  and and_5 (and_5_out, Q2_q, Q1_q, random_1_out);
  and and_6 (and_6_out, not_1_out, not_2_out, Q0_q, random_1_out);
  and and_7 (and_7_out, not_1_out, Q1_q, random_1_out);
  and and_8 (and_8_out, Q2_q, not_2_out, random_1_out);
  and and_9 (and_9_out, Q2_q, Q1_q, random_1_out);
  and and_10 (and_10_out, not_1_out, Q1_q, Q0_q, random_1_out);
  and and_11 (and_11_out, Q2_q, not_2_out, Q0_q, random_1_out);
  and and_12 (and_12_out, Q2_q, Q1_q, not_3_out, random_1_out);
  or or_1 (or_1_out, and_1_out, and_2_out, and_3_out, and_4_out, and_5_out);
  or or_2 (or_2_out, and_6_out, and_7_out, and_8_out, and_9_out);
  or or_3 (or_3_out, and_10_out, and_11_out, and_12_out);
  D_Flip_Flop Q0 (.D(or_1_out), .clk(CLK), .Q(Q0_q));  // open: Qn, preset, reset
  D_Flip_Flop Q1 (.D(or_2_out), .clk(CLK), .Q(Q1_q));  // open: Qn, preset, reset
  D_Flip_Flop Q2 (.D(or_3_out), .clk(CLK), .Q(Q2_q));  // open: Qn, preset, reset
  and and_13 (and_13_out, Q0_q, Q1_q, Q2_q);
  // Buzzer buzzer_1: pin names not known; wires that end beside it: and_13_out
endmodule
