// Logisim project 01_RAM.circ as structural Verilog: 1 circuit, main circuit main
module main (
  input  Clear,
  input  [11:0] Addr,
  input  [1:0] Enable,
  input  [31:0] DataIn,
  input  [1:0] Mode,
  output [31:0] out_6,
  output [31:0] out_7
);

  wire Clk_out;
  wire [7:0] multiplexer_2_out;
  wire [15:0] multiplexer_3_out;
  wire [31:0] ram_1_dout;

  Multiplexer #(.select(2), .width(32)) multiplexer_1 (
    .in0({{24{1'b0}}, DataIn[7:0]}), .in1({{16{1'b0}}, DataIn[15:0]}), .in2(DataIn), .in3(DataIn),
    .out(out_7), .sel(Mode));
  Clock Clk (.out(Clk_out));
  RAM #(.addrWidth(10), .clearpin("true"), .dataWidth(32)) ram_1 (
    .addr(Addr[11:2]), .we(Enable[0]), .oe(Enable[1]), .clk(Clk_out), .din(out_7), .dout(ram_1_dout),
    .clr(Clear));
  Multiplexer #(.select(2), .width(8)) multiplexer_2 (
    .in0(ram_1_dout[7:0]), .in1(ram_1_dout[15:8]), .in2(ram_1_dout[23:16]), .in3(ram_1_dout[31:24]),
    .out(multiplexer_2_out), .sel(Addr[1:0]));
  Multiplexer #(.width(16)) multiplexer_3 (
    .in0(ram_1_dout[15:0]), .in1(ram_1_dout[31:16]), .out(multiplexer_3_out), .sel(Addr[1]));
  Multiplexer #(.select(2), .width(32)) multiplexer_4 (
    .in0({{24{1'b0}}, multiplexer_2_out}), .in1({{16{1'b0}}, multiplexer_3_out}), .in2(ram_1_dout),
    .in3(ram_1_dout), .out(out_6), .sel(Mode));
endmodule
